// Logisim project cpu_large_screen.circ as structural Verilog: 1 circuit, main circuit main
module main (
);

  wire and_1_out, and_2_out, bcd_to_7_segment_decoder_3_p1, binary_to_bcd_converter_1_p2,
       binary_to_bcd_converter_1_p4, BRS, BRZ, clock_1_out, clock_3_out, clock_4_out, clock_5_out,
       clock_6_out, clock_7_out, clock_8_out, clock_9_out, clock_10_out, CPC, EIR, EPC, ER1, ERAM, ERT, LIR,
       LM, LPC, LR1, LR2, LRAM, LRO, or_1_out, REN, rgb_video_1_p1, SIGN, SUB, ZERO;
  wire [0:0] MICROCODE_data;
  wire [3:0] counter_2_q, MEMORY_data_2, rgb_video_1_p5;
  wire [3:3] MEMORY_data;
  wire [4:0] rgb_video_1_p4;
  wire [5:0] rgb_video_1_p3;
  wire [7:0] multiplexer_3_out, negator_1_out, register_1_q;
  wire [15:0] adder_1_out, bit_extender_1_out, counter_1_q, IR_q, MAR_q, multiplexer_2_out, negator_2_out,
       R1_q, R2_q, register_2_q;

  Register #(.width(16)) MAR (
    .D({MEMORY_data_2, MEMORY_data[3], rgb_video_1_p4, rgb_video_1_p3}), .en(LM), .Q(MAR_q), .clk(clock_1_out));  // open: clr
  Clock clock_1 (.out(clock_1_out));
  // RGB_Video #(.cursor("No Cursor"), .height(32), .scale(4), .width(64)) rgb_video_1: pin names not known; wires that end beside it: rgb_video_1_p1, REN, rgb_video_1_p3, rgb_video_1_p4, rgb_video_1_p5
  Clock clock_2 (.out(rgb_video_1_p1));
  RAM #(.addrWidth(16), .dataWidth(16), .databus("bidir"), .\type ("nonvolatile")) MEMORY (
    .addr(MAR_q), .we(LRAM), .oe(ERAM), .clk(clock_3_out),
    .data({MEMORY_data_2, MEMORY_data[3], rgb_video_1_p4, rgb_video_1_p3}));
  Clock clock_3 (.out(clock_3_out));
  Multiplexer #(.width(4)) multiplexer_1 (.in0(4'b1111), .in1(4'b0000), .out(rgb_video_1_p5), .sel(MEMORY_data[3]));
  Hex_Digit_Display #(.decimalPoint("false")) hex_digit_display_1 (.value(MEMORY_data_2));
  and and_1 (and_1_out, ZERO, BRZ);
  and and_2 (and_2_out, SIGN, BRS);
  Hex_Digit_Display #(.decimalPoint("false")) hex_digit_display_2 (.value({MEMORY_data[3], rgb_video_1_p4[4:2]}));
  Hex_Digit_Display #(.decimalPoint("false")) hex_digit_display_3 (.value({rgb_video_1_p4[1:0], rgb_video_1_p3[5:4]}));
  or or_1 (or_1_out, and_1_out, LPC, and_2_out);
  Hex_Digit_Display #(.decimalPoint("false")) hex_digit_display_4 (.value(rgb_video_1_p3[3:0]));
  assign {MEMORY_data_2, MEMORY_data[3], rgb_video_1_p4, rgb_video_1_p3} = EPC ? counter_1_q : 16'bz;  // Controlled_Buffer controlled_buffer_1
  Counter #(.max('hffff), .width(16)) counter_1 (
    .load(or_1_out), .D({MEMORY_data_2, MEMORY_data[3], rgb_video_1_p4, rgb_video_1_p3}), .count(CPC),
    .Q(counter_1_q), .up(1'b1), .clk(clock_4_out));  // open: carry, clr
  Clock clock_4 (.out(clock_4_out));
  assign {MEMORY_data_2, MEMORY_data[3], rgb_video_1_p4, rgb_video_1_p3} = ER1 ? R1_q : 16'bz;  // Controlled_Buffer controlled_buffer_2
  Clock clock_5 (.out(clock_5_out));
  Clock clock_6 (.out(clock_6_out));
  Clock clock_7 (.out(clock_7_out));
  Clock clock_8 (.out(clock_8_out));
  Register #(.width(16)) R1 (
    .D({MEMORY_data_2, MEMORY_data[3], rgb_video_1_p4, rgb_video_1_p3}), .en(LR1), .Q(R1_q), .clk(clock_5_out));  // open: clr
  Register #(.width(16)) R2 (
    .D({MEMORY_data_2, MEMORY_data[3], rgb_video_1_p4, rgb_video_1_p3}), .en(LR2), .Q(R2_q), .clk(clock_6_out));  // open: clr
  Register #(.width(16)) IR (
    .D({MEMORY_data_2, MEMORY_data[3], rgb_video_1_p4, rgb_video_1_p3}), .en(LIR), .Q(IR_q), .clk(clock_7_out));  // open: clr
  assign {MEMORY_data_2, MEMORY_data[3], rgb_video_1_p4, rgb_video_1_p3} = EIR ? bit_extender_1_out : 16'bz;  // Controlled_Buffer controlled_buffer_3
  Register register_1 (
    .D({rgb_video_1_p4[1:0], rgb_video_1_p3}), .en(LRO), .Q(register_1_q), .clk(clock_8_out));  // open: clr
  Negator negator_1 (.in(register_1_q), .out(negator_1_out));
  Comparator #(.width(16)) comparator_1 (.a({16{1'b0}}), .b(R1_q), .gt(SIGN), .eq(ZERO));  // open: lt
  Multiplexer #(.width(16)) multiplexer_2 (.in0(R2_q), .in1(negator_2_out), .out(multiplexer_2_out), .sel(SUB));
  Negator #(.width(16)) negator_2 (.in(R2_q), .out(negator_2_out));
  assign bit_extender_1_out = {{4{1'b0}}, IR_q[11:0]};  // Bit_Extender bit_extender_1
  Multiplexer #(.width(8)) multiplexer_3 (
    .in0(register_1_q), .in1(negator_1_out), .out(multiplexer_3_out), .sel(register_1_q[7]));
  Adder #(.width(16)) adder_1 (.a(R1_q), .b(multiplexer_2_out), .out(adder_1_out));  // open: cin, cout
  ROM #(.dataWidth(18)) MICROCODE (
    .addr({IR_q[15:12], counter_2_q}),
    .data({REN, EIR, LIR, ERT, BRS, LR2, ER1, LR1, EPC, LPC, LM, LRAM, ERAM, CPC, LRO, SUB, BRZ, MICROCODE_data[0]}));
  Counter #(.max('hf), .width(4)) counter_2 (
    .Q(counter_2_q), .up(1'b1), .clk(clock_9_out), .clr(MICROCODE_data[0]));  // open: load, D, count, carry
  Clock clock_9 (.out(clock_9_out));
  _7_Segment_Display u_7_segment_display_1 (.g(register_1_q[7]));  // open: f, a, b, e, d, c, dp
  _7_Segment_Display u_7_segment_display_2 ();  // open: g, f, a, b, e, d, c, dp
  // BCD_to_7_Segment_decoder bcd_to_7_segment_decoder_1: pin names not known
  // Binary_to_BCD_converter #(.binvalue(8)) binary_to_bcd_converter_1: pin names not known; wires that end beside it: multiplexer_3_out, binary_to_bcd_converter_1_p2, binary_to_bcd_converter_1_p2, binary_to_bcd_converter_1_p4
  assign {MEMORY_data_2, MEMORY_data[3], rgb_video_1_p4, rgb_video_1_p3} = ERT ? register_2_q : 16'bz;  // Controlled_Buffer controlled_buffer_4
  Register #(.width(16)) register_2 (.D(adder_1_out), .en(1'b1), .Q(register_2_q), .clk(clock_10_out));  // open: clr
  Clock clock_10 (.out(clock_10_out));
  _7_Segment_Display u_7_segment_display_3 ();  // open: g, f, a, b, e, d, c, dp
  // BCD_to_7_Segment_decoder bcd_to_7_segment_decoder_2: pin names not known; wires that end beside it: binary_to_bcd_converter_1_p4
  _7_Segment_Display u_7_segment_display_4 ();  // open: g, f, a, b, e, d, c, dp
  // BCD_to_7_Segment_decoder bcd_to_7_segment_decoder_3: pin names not known; wires that end beside it: bcd_to_7_segment_decoder_3_p1, bcd_to_7_segment_decoder_3_p1

  // Notes on the sheet:
  //   PC
  //   ALU
  //   contents of MICROCODE (hex, n*v repeats v):
  //   280 20 8020 10 10080 20 420 1 8*0 280 20 8020 10 10080 840 1 9*0 280 20 8020 10 10080 20 a0 20 420 1
  //   6*0 280 20 8020 10 10080 20 a0 840 1 7*0 280 20 8020 10 10080 20 1020 0 4400 1 6*0 280 20 8020 10
  //   10080 20 1020 4 4400 1 6*0 280 20 8020 10 10100 1 10*0 280 20 8020 10 10002 1 10*0 280 20 8020 10
  //   12000 1 10*0 280 20 8020 10 808 1 10*0 280 20 8020 10 30000 1
  //   OUTPUT
endmodule
